# Fritzing sketch esquema (saved by Fritzing 0.9.3b)

parts:
  Componente1 = Arduino Uno (Rev3)
  RHT2 = Humidity and Temperature Sensor RHT03 [part_number=DHT22]
  R1 = Resistor [tolerance=±5% resistance=10k package="2010 [SMD]"]

nets:
  N1: Componente1.D2, RHT2.Data-signal, R1.Pin_1
  5V: Componente1.5V, RHT2.Vcc, R1.Pin_0
  N2: Componente1.GND, RHT2.GND_2

notes:
  Colocar resistencia 10K si no está encapsulada en el DHT22
